// Logisim project Cpu.circ as structural Verilog: 4 circuits, main circuit register_file
module register_file (
  input  Write,
  input  [2:0] Write_Register,
  input  [15:0] Write_DATA,
  input  [2:0] Read_Register2,
  input  [2:0] Read_Register1,
  input  clock,
  input  reset,
  output [15:0] Read_Data_1,
  output [15:0] Read_Data_2
);

  wire and_1_out, and_2_out, and_3_out, and_4_out, and_5_out, and_6_out, and_7_out, and_8_out,
       decoder_1_out0, decoder_1_out1, decoder_1_out2, decoder_1_out3, decoder_1_out4, decoder_1_out5,
       decoder_1_out6, decoder_1_out7, undriven;
  wire [15:0] Register1_q, Register_2_q, Register_3_q, Register_4_q, Register_5_q, Register_6_q,
       Register_7_q, Register_8_q;

  Decoder #(.enable("false"), .select(3)) decoder_1 (
    .out0(decoder_1_out0), .out1(decoder_1_out1), .out2(decoder_1_out2), .out3(decoder_1_out3),
    .out4(decoder_1_out4), .out5(decoder_1_out5), .out6(decoder_1_out6), .out7(decoder_1_out7),
    .sel(Write_Register));
  and and_1 (and_1_out, Write, decoder_1_out2);
  and and_2 (and_2_out, Write, decoder_1_out5);
  and and_3 (and_3_out, Write, decoder_1_out7);
  and and_4 (and_4_out, Write, decoder_1_out0);
  and and_5 (and_5_out, Write, decoder_1_out1);
  and and_6 (and_6_out, Write, decoder_1_out4);
  and and_7 (and_7_out, Write, decoder_1_out3);
  and and_8 (and_8_out, Write, decoder_1_out6);
  Register #(.width(16)) Register_3 (.D(Write_DATA), .en(and_1_out), .clk(clock), .Q(Register_3_q), .clr(reset));
  Register #(.width(16)) Register_4 (.D(Write_DATA), .en(and_7_out), .clk(clock), .Q(Register_4_q), .clr(reset));
  Register #(.width(16)) Register_5 (.D(Write_DATA), .en(and_6_out), .clk(clock), .Q(Register_5_q), .clr(reset));
  Register #(.width(16)) Register_6 (.D(Write_DATA), .en(and_2_out), .clk(clock), .Q(Register_6_q), .clr(reset));
  Register #(.width(16)) Register1 (.D(Write_DATA), .en(and_4_out), .clk(clock), .Q(Register1_q), .clr(reset));
  Register #(.width(16)) Register_7 (.D(Write_DATA), .en(and_8_out), .clk(clock), .Q(Register_7_q), .clr(reset));
  Register #(.width(16)) Register_8 (.D(Write_DATA), .en(and_3_out), .clk(clock), .Q(Register_8_q), .clr(reset));
  Register #(.width(16)) Register_2 (.D(Write_DATA), .en(and_5_out), .clk(clock), .Q(Register_2_q), .clr(reset));
  Multiplexer #(.select(3), .width(16)) multiplexer_1 (
    .in0(Register1_q), .in1(Register_2_q), .in2(Register_3_q), .in3(Register_4_q), .in4(Register_5_q),
    .in5(Register_6_q), .in6(Register_7_q), .in7(Register_8_q), .out(Read_Data_2), .sel(Read_Register1),
    .en(undriven));
  Multiplexer #(.select(3), .width(16)) multiplexer_2 (
    .in0(Register1_q), .in1(Register_2_q), .in2(Register_3_q), .in3(Register_4_q), .in4(Register_5_q),
    .in5(Register_6_q), .in6(Register_7_q), .in7(Register_8_q), .out(Read_Data_1), .sel(Read_Register2),
    .en(undriven));
endmodule

module ALU (
  input  [15:0] in1,
  input  [15:0] in2,
  input  ALU_Ouput0,
  input  ALU_Output1,
  output branch,
  output [15:0] aluOut
);

  wire and_2_out, and_3_out, comparator_1_eq, comparator_1_lt, not_1_out, or_2_out;
  wire [15:0] adder_1_out, and_1_out, or_1_out;

  Comparator #(.width(16)) comparator_1 (.a(in1), .b(in2), .eq(comparator_1_eq), .lt(comparator_1_lt));  // open: gt
  assign or_1_out = in1 | in2;  // OR_Gate or_1, 16 bits wide
  assign and_1_out = in1 & in2;  // AND_Gate and_1, 16 bits wide
  Adder #(.width(16)) adder_1 (.a(in1), .b(in2), .out(adder_1_out));  // open: cin, cout
  not not_1 (not_1_out, comparator_1_eq);
  or or_2 (or_2_out, comparator_1_eq, comparator_1_lt);
  Multiplexer #(.enable("false"), .select(2), .width(16)) multiplexer_1 (
    .in0(and_1_out), .in1(or_1_out), .in2(adder_1_out), .out(aluOut), .sel({ALU_Output1, ALU_Ouput0}));  // open: in3
  and and_2 (and_2_out, not_1_out, ALU_Output1);
  and and_3 (and_3_out, or_2_out, ALU_Ouput0);
  or or_3 (branch, and_2_out, and_3_out);
endmodule

module main (
);

  wire and_1_out, and_2_out, br, call, clock_1_out, cmpr, control_unit_1_alu_op0, control_unit_1_alu_op1,
       halt, jmp, li, m2r, mr, mw, not_1_out, op3, or_1_out, rd, rtn, rw, src;
  wire [2:0] multiplexer_1_out, rom_1_data_2;
  wire [15:0] adder_1_out, adder_2_out, alu_1_aluout, immd, multiplexer_2_out, multiplexer_3_out,
       multiplexer_4_out, multiplexer_6_out, ra_q, ram_1_dout, register_1_q, register_file_1_read_data_1,
       register_file_1_read_data_2, rom_1_data, wd;

  Clock clock_1 (.out(clock_1_out));
  not not_1 (not_1_out, halt);
  Register #(.width(16)) register_1 (.D(multiplexer_6_out), .en(1'b1), .clk(and_1_out), .Q(register_1_q));  // open: clr
  and and_1 (and_1_out, clock_1_out, not_1_out);
  ROM #(.addrWidth(16), .dataWidth(16)) rom_1 (
    .addr(register_1_q), .data({rom_1_data[15:14], op3, rom_1_data_2, rom_1_data[9:0]}));
  assign immd = {{10{rom_1_data[3]}}, {rom_1_data[3:1], rom_1_data[15:14], rom_1_data[0]}};  // Bit_Extender bit_extender_1
  Multiplexer #(.enable("false"), .width(3)) multiplexer_1 (
    .in0(rom_1_data[6:4]), .in1(rom_1_data[3:1]), .out(multiplexer_1_out), .sel(rd));
  control_unit control_unit_1 (
    .op3(op3), .op2(rom_1_data_2[2]), .op1(rom_1_data_2[1]), .op0(rom_1_data_2[0]),
    .alu_op1(control_unit_1_alu_op1), .alu_op0(control_unit_1_alu_op0), .reg_dest(rd), .alu_src(src),
    .limmd(li), .m2r(m2r), .rw(rw), .mr(mr), .mw(mw), .branch(br), .call(call), .rtn(rtn), .jmp(jmp),
    .halt(halt));
  register_file register_file_1 (
    .Write(rw), .Write_Register(multiplexer_1_out), .Write_DATA(wd), .Read_Register2(rom_1_data[9:7]),
    .Read_Register1(rom_1_data[6:4]), .clock(and_1_out), .reset(1'b0),
    .Read_Data_1(register_file_1_read_data_1), .Read_Data_2(register_file_1_read_data_2));
  Multiplexer #(.enable("false"), .width(16)) multiplexer_2 (
    .in0(register_file_1_read_data_2), .in1(immd), .out(multiplexer_2_out), .sel(src));
  Multiplexer #(.enable("false"), .width(16)) multiplexer_3 (
    .in0(register_file_1_read_data_1), .in1({16{1'b0}}), .out(multiplexer_3_out), .sel(li));
  and and_2 (and_2_out, br, cmpr);
  or or_1 (or_1_out, and_2_out, jmp, rtn, call);
  ALU alu_1 (
    .in1(multiplexer_3_out), .in2(multiplexer_2_out), .ALU_Ouput0(control_unit_1_alu_op0),
    .ALU_Output1(control_unit_1_alu_op1), .branch(cmpr), .aluOut(alu_1_aluout));
  Multiplexer #(.enable("false"), .width(16)) multiplexer_4 (
    .in0(16'h1), .in1(immd), .out(multiplexer_4_out), .sel(or_1_out));
  Adder #(.width(16)) adder_1 (.a(register_1_q), .b(multiplexer_4_out), .out(adder_1_out));  // open: cin, cout
  Adder #(.width(16)) adder_2 (.a(register_1_q), .b(16'h1), .out(adder_2_out));  // open: cin, cout
  Multiplexer #(.enable("false"), .width(16)) multiplexer_5 (.in0(alu_1_aluout), .in1(ram_1_dout), .out(wd), .sel(m2r));
  RAM #(.addrWidth(16), .asyncread("true"), .dataWidth(16), .\type ("nonvolatile")) ram_1 (
    .addr(alu_1_aluout), .we(mw), .oe(mr), .clk(and_1_out), .din(register_file_1_read_data_2),
    .dout(ram_1_dout));
  Register #(.width(16)) ra (.D(adder_2_out), .en(call), .clk(and_1_out), .Q(ra_q));  // open: clr
  Multiplexer #(.enable("false"), .width(16)) multiplexer_6 (
    .in0(adder_1_out), .in1(ra_q), .out(multiplexer_6_out), .sel(rtn));

  // Notes on the sheet:
  //   contents of rom_1 (hex, n*v repeats v):
  //   dc00 9c10 e801 1930 dc01 1c12 6801 1940 6001 3814 2400 3c00
endmodule

module control_unit (
  input  op3,
  input  op2,
  input  op1,
  input  op0,
  output alu_op1,
  output alu_op0,
  output reg_dest,
  output alu_src,
  output limmd,
  output m2r,
  output rw,
  output mr,
  output mw,
  output branch,
  output call,
  output rtn,
  output jmp,
  output halt
);

  wire and_1_out, and_2_out, and_3_out, and_4_out, and_5_out, and_6_out, and_7_out, and_8_out, and_9_out,
       and_10_out, and_11_out, and_12_out, and_13_out, and_14_out, and_15_out, and_16_out, and_17_out,
       and_18_out, and_19_out, not_1_out, or_1_out, or_2_out, or_3_out, or_4_out, or_5_out, or_6_out,
       or_7_out, or_8_out;

  and and_1 (and_1_out, op2, ~op0);  // AND_Gate
  and and_2 (and_2_out, ~op3, ~op2, op0);  // AND_Gate
  or or_1 (or_1_out, and_1_out, and_2_out);
  or or_2 (or_2_out, ~op1, ~op0);  // OR_Gate
  and and_3 (and_3_out, op3, op2);
  and and_4 (and_4_out, op0, op2);
  and and_5 (and_5_out, ~op2, or_2_out);  // AND_Gate
  and and_6 (and_6_out, op1, or_1_out);
  or or_3 (or_3_out, and_4_out, and_5_out);
  and and_7 (and_7_out, or_3_out, ~op3);  // AND_Gate
  and and_8 (and_8_out, op2, ~op1, op0);  // AND_Gate
  or or_4 (or_4_out, ~op1, ~op0);  // OR_Gate
  and and_9 (and_9_out, ~op3, ~op1, ~op0);  // AND_Gate
  and and_10 (and_10_out, ~op3, op1);  // AND_Gate
  and and_11 (and_11_out, op3, or_4_out);
  or or_5 (or_5_out, and_7_out, and_8_out);
  or or_6 (or_6_out, and_10_out, and_11_out);
  or or_7 (or_7_out, op2, ~op1);  // OR_Gate
  and and_12 (and_12_out, op2, op1, op0);
  and and_13 (and_13_out, ~op3, ~op2, ~op1, ~op0);  // AND_Gate
  or or_8 (or_8_out, op2, and_9_out);
  and and_14 (and_14_out, ~op3, ~op2, ~op1, op0);  // AND_Gate
  and and_15 (and_15_out, ~op3, or_7_out);  // AND_Gate
  and and_16 (and_16_out, ~op2, or_6_out);  // AND_Gate
  and and_17 (and_17_out, op3, ~op2, op1, ~op0);  // AND_Gate
  and and_18 (and_18_out, op3, ~op2, ~op1, op0);  // AND_Gate
  and and_19 (and_19_out, op3, ~op2, ~op1, ~op0);  // AND_Gate
  and and_20 (halt, op3, op2, op1, op0);
  not not_1 (not_1_out, halt);
  and and_21 (alu_op1, and_6_out, not_1_out);
  and and_22 (alu_op0, or_5_out, not_1_out);
  and and_23 (reg_dest, and_3_out, not_1_out);
  and and_24 (alu_src, and_15_out, not_1_out);
  and and_25 (limmd, and_12_out, not_1_out);
  and and_26 (m2r, and_13_out, not_1_out);
  and and_27 (rw, or_8_out, not_1_out);
  and and_28 (mr, and_13_out, not_1_out);
  and and_29 (mw, and_14_out, not_1_out);
  and and_30 (branch, and_16_out, not_1_out);
  and and_31 (call, and_17_out, not_1_out);
  and and_32 (rtn, and_18_out, not_1_out);
  and and_33 (jmp, and_19_out, not_1_out);
endmodule
